// Logisim project Fifth processor.circ as structural Verilog: 8 circuits, main circuit main
module main (
);

  ProcFifth procfifth_1 ();  // open: stack_top

  // Notes on the sheet:
  //   ATALLA Salim
  //   NISO Aram
  //   Groupe 584I
endmodule

module Pile (
  input  [1:0] SPsel,
  input  clk,
  input  [1:0] Wsel,
  input  [15:0] Input,
  output [15:0] stack_SP,
  output [15:0] stack_SP_1
);

  wire _0, _1, _2, _3, _4, _5, _6, _7, _8, _9, _10, _11, _12, _13, _14, _15, nand_1_out;
  wire [3:0] multiplexer_1_out, OutSP, SelDMX, SP_1, SP_1_t;
  wire [15:0] r0_q, r1_q, r2_q, r3_q, r4_q, r5_q, r6_q, r7_q, r8_q, r9_q, r10_q, r11_q, r12_q, r13_q, r14_q,
       r15_q;

  nand nand_1 (nand_1_out, Wsel[0], Wsel[1]);
  Demultiplexer #(.select(4), .enable("false")) demultiplexer_1 (
    .out0(_0), .out1(_1), .out2(_2), .out3(_3), .out4(_4), .out5(_5), .out6(_6), .out7(_7), .out8(_8),
    .out9(_9), .out10(_10), .out11(_11), .out12(_12), .out13(_13), .out14(_14), .out15(_15), .in(nand_1_out),
    .sel(SelDMX));
  Subtractor #(.width(4)) subtractor_1 (.a(OutSP), .b(4'b0001), .out(SP_1_t));  // open: bin, bout
  Adder #(.width(4)) adder_1 (.a(4'b0001), .b(OutSP), .out(SP_1));  // open: cin, cout
  Multiplexer #(.select(2), .width(4), .enable("false")) multiplexer_1 (
    .in0(4'b0000), .in1(SP_1), .in2(OutSP), .in3(SP_1_t), .out(multiplexer_1_out), .sel(SPsel));
  Multiplexer #(.select(2), .width(4), .enable("false")) multiplexer_2 (
    .in0(OutSP), .in1(SP_1_t), .in2(SP_1), .in3(SelDMX), .out(SelDMX), .sel(Wsel));
  Register #(.width(4)) SP (.D(multiplexer_1_out), .en(1'b1), .Q(OutSP), .clk(clk));  // open: clr
  Register #(.width(16)) r0 (.D(Input), .en(_0), .Q(r0_q), .clk(clk));  // open: clr
  Register #(.width(16)) r1 (.D(Input), .en(_1), .Q(r1_q), .clk(clk));  // open: clr
  Register #(.width(16)) r2 (.D(Input), .en(_2), .Q(r2_q), .clk(clk));  // open: clr
  Register #(.width(16)) r3 (.D(Input), .en(_3), .Q(r3_q), .clk(clk));  // open: clr
  Register #(.width(16)) r4 (.D(Input), .en(_4), .Q(r4_q), .clk(clk));  // open: clr
  Register #(.width(16)) r5 (.D(Input), .en(_5), .Q(r5_q), .clk(clk));  // open: clr
  Register #(.width(16)) r6 (.D(Input), .en(_6), .Q(r6_q), .clk(clk));  // open: clr
  Register #(.width(16)) r7 (.D(Input), .en(_7), .Q(r7_q), .clk(clk));  // open: clr
  Register #(.width(16)) r8 (.D(Input), .en(_8), .Q(r8_q), .clk(clk));  // open: clr
  Register #(.width(16)) r9 (.D(Input), .en(_9), .Q(r9_q), .clk(clk));  // open: clr
  Register #(.width(16)) r10 (.D(Input), .en(_10), .Q(r10_q), .clk(clk));  // open: clr
  Register #(.width(16)) r11 (.D(Input), .en(_11), .Q(r11_q), .clk(clk));  // open: clr
  Register #(.width(16)) r12 (.D(Input), .en(_12), .Q(r12_q), .clk(clk));  // open: clr
  Register #(.width(16)) r13 (.D(Input), .en(_13), .Q(r13_q), .clk(clk));  // open: clr
  Register #(.width(16)) r14 (.D(Input), .en(_14), .Q(r14_q), .clk(clk));  // open: clr
  Register #(.width(16)) r15 (.D(Input), .en(_15), .Q(r15_q), .clk(clk));  // open: clr
  Multiplexer #(.select(4), .width(16)) multiplexer_3 (
    .in0(r0_q), .in1(r1_q), .in2(r2_q), .in3(r3_q), .in4(r4_q), .in5(r5_q), .in6(r6_q), .in7(r7_q),
    .in8(r8_q), .in9(r9_q), .in10(r10_q), .in11(r11_q), .in12(r12_q), .in13(r13_q), .in14(r14_q),
    .in15(r15_q), .out(stack_SP), .sel(OutSP));  // open: en
  Multiplexer #(.select(4), .width(16), .enable("false")) multiplexer_4 (
    .in0(r15_q), .in1(r0_q), .in2(r1_q), .in3(r2_q), .in4(r3_q), .in5(r4_q), .in6(r5_q), .in7(r6_q),
    .in8(r7_q), .in9(r8_q), .in10(r9_q), .in11(r10_q), .in12(r11_q), .in13(r12_q), .in14(r13_q),
    .in15(r14_q), .out(stack_SP_1), .sel(SP_1_t));
endmodule

module ALU (
  input  [15:0] A,
  input  [5:0] Op,
  input  [15:0] B,
  output [15:0] C,
  output [2:0] out_5,
  output out_6
);

  wire and_1_out, and_2_out, bitselector_1_out, bitselector_2_out, bitselector_3_out, bitselector_4_out,
       not_1_out;
  wire [15:0] adder_1_out, divider_1_out, divider_1_rem, ET_out, multiplier_1_out, negator_1_out, Non_out,
       not_2_out, OU_out, shifter_1_out, shifter_2_out, subtractor_1_out;

  BitSelector #(.width(16)) bitselector_1 (.in(A), .out(bitselector_1_out), .sel(4'b1111));
  BitSelector #(.width(16)) bitselector_2 (.in(B), .out(bitselector_2_out), .sel(4'b1111));
  BitSelector #(.width(16)) bitselector_3 (.in(A), .out(bitselector_3_out), .sel(4'b1111));
  BitSelector #(.width(16)) bitselector_4 (.in(B), .out(bitselector_4_out), .sel(4'b1111));
  not not_1 (not_1_out, bitselector_4_out);
  Adder #(.width(16)) adder_1 (.a(A), .b(B), .out(adder_1_out), .cout(out_6));  // open: cin
  Subtractor #(.width(16)) subtractor_1 (.a(A), .b(B), .out(subtractor_1_out), .bout(out_6));  // open: bin
  Negator #(.width(16)) negator_1 (.in(A), .out(negator_1_out));
  Multiplier #(.width(16)) multiplier_1 (.a(A), .b(B), .out(multiplier_1_out));  // open: cin, cout
  Divider #(.width(16)) divider_1 (.a(A), .b(B), .out(divider_1_out), .rem(divider_1_rem));  // open: upper
  assign Non_out = ~A;  // NOT_Gate Non, 16 bits wide
  assign ET_out = A & B;  // AND_Gate ET, 16 bits wide
  assign OU_out = A | B;  // OR_Gate OU, 16 bits wide
  Shifter #(.width(16)) shifter_1 (.in(A), .\dist (4'b0001), .out(shifter_1_out));
  Shifter #(.width(16), .shift("lr")) shifter_2 (.in(A), .\dist (4'b0001), .out(shifter_2_out));
  and and_1 (and_1_out, bitselector_1_out, bitselector_2_out);
  and and_2 (and_2_out, bitselector_3_out, not_1_out);
  or or_1 (out_5[0], and_1_out, and_2_out);
  Multiplexer #(.select(4), .width(16)) multiplexer_1 (
    .in0(adder_1_out), .in1(subtractor_1_out), .in2(negator_1_out), .in3(multiplier_1_out),
    .in4(divider_1_out), .in5(divider_1_rem), .in6(Non_out), .in7(ET_out), .in8(OU_out), .in9(shifter_1_out),
    .in10(shifter_2_out), .out(C), .sel(Op[3:0]));  // open: in11, in12, in13, in14, in15, en
  and FZ (out_5[2], not_2_out[0], not_2_out[1], not_2_out[2], not_2_out[3], not_2_out[4], not_2_out[5], not_2_out[6], not_2_out[8], not_2_out[9], not_2_out[10], not_2_out[11], not_2_out[12], not_2_out[13], not_2_out[14], not_2_out[15]);
  assign not_2_out = ~C;  // NOT_Gate not_2, 16 bits wide

  assign out_5[1] = C[15];

  // Other names for the same wires on the sheet: Flags[2:0] = {out_5[2], C[15], out_5[0]}; SF = C[15]; Cbout = out_6;
  //   OF = out_5[0]; ZF = out_5[2]; op_t[3:0] = Op[3:0]
endmodule

module Testeur (
  input  [5:0] Op,
  input  [2:0] Flags,
  output [15:0] S
);

  wire OF1;

  nor nor_1 (OF1, Flags[2], Flags[1]);
  Multiplexer #(.select(2)) multiplexer_1 (
    .in0(Flags[2]), .in1(OF1), .in3(Flags[1]), .out(S[15]), .sel(Op[5:4]));  // open: in2, en

  assign S[14:0] = {15{S[15]}};

  // Other names for the same wires on the sheet: OF = Flags[0]; SF = Flags[1]; ZF = Flags[2]; sel[1:0] = Op[5:4]
endmodule

module MAJPC (
  input  [15:0] saut_call,
  input  [15:0] PC,
  input  [15:0] Stack,
  input  [1:0] Signial,
  output [15:0] Sortie,
  output [15:0] PC_1
);

  Adder #(.width(16)) adder_1 (.a(PC), .b(16'h1), .out(PC_1));  // open: cin, cout
  Multiplexer #(.select(2), .width(16)) multiplexer_1 (
    .in0(PC_1), .in1(saut_call), .in2(saut_call), .in3(Stack), .out(Sortie), .sel(Signial));  // open: en
endmodule

module Controleur (
  input  [5:0] Op,
  output [1:0] SPsel,
  output [1:0] Wsel,
  output [1:0] SPselC,
  output [1:0] WselC
);

  ROM #(.addrWidth(6)) rom_1 (.addr(Op), .data({WselC, SPselC, Wsel, SPsel}));  // open: sel
endmodule

module ProcFifth (
  input  [15:0] stack_top
);

  wire Clk;
  wire [1:0] controleur_1_spsel, controleur_1_spselc, controleur_1_wsel, controleur_1_wselc;
  wire [2:0] alu_1_out_5, undriven_2;
  wire [5:0] OpCode;
  wire [9:0] val_adr;
  wire [15:0] alu_1_c, majpc_1_sortie, multiplexer_1_out, pc_1_output, pile_1_stack_sp, pile_2_stack_sp,
       pile_2_stack_sp_1, testeur_1_s, undriven, valRam;
  wire [15:10] undriven_3;

  ROM #(.addrWidth(16), .dataWidth(16)) rom_1 (.addr(majpc_1_sortie), .data({val_adr, OpCode}));  // open: sel
  RAM #(.addrWidth(16), .dataWidth(16)) ram_1 (.addr(undriven), .data(valRam));  // open: sel, clk, ld, clr
  Multiplexer #(.select(3), .width(16)) multiplexer_1 (
    .in3(stack_top), .in4(valRam), .in5({undriven_3, val_adr}), .in6(alu_1_c), .in7(testeur_1_s),
    .out(multiplexer_1_out), .sel(undriven_2));  // open: in0, in1, in2, en
  Pile pile_1 (
    .SPsel(controleur_1_spselc), .stack_SP(pile_1_stack_sp), .clk(Clk), .Wsel(controleur_1_wselc));  // open: Input, stack_SP_1
  Pile pile_2 (
    .SPsel(controleur_1_spsel), .Input(multiplexer_1_out), .stack_SP(pile_2_stack_sp),
    .stack_SP_1(pile_2_stack_sp_1), .clk(Clk), .Wsel(controleur_1_wsel));
  PC pc_1 (.Input(majpc_1_sortie), .Output(pc_1_output), .Clk(Clk));
  Controleur controleur_1 (
    .Op(OpCode), .SPsel(controleur_1_spsel), .Wsel(controleur_1_wsel), .SPselC(controleur_1_spselc),
    .WselC(controleur_1_wselc));
  MAJPC majpc_1 (.PC(pc_1_output), .Sortie(majpc_1_sortie), .Stack(pile_1_stack_sp));  // open: saut_call, PC_1, Signial
  ALU alu_1 (.A(pile_2_stack_sp), .B(pile_2_stack_sp_1), .C(alu_1_c), .Op(OpCode), .out_5(alu_1_out_5));  // open: out_6
  Testeur testeur_1 (.S(testeur_1_s), .Flags(alu_1_out_5), .Op(OpCode));
  Clock u_Clk (.out(Clk));
endmodule

module PC (
  input  [15:0] Input,
  input  Clk,
  output [15:0] Output
);

  Register #(.width(16)) PC (.D(Input), .en(1'b1), .Q(Output), .clk(Clk));  // open: clr
endmodule
